# Fritzing sketch grill temp monitor (saved by Fritzing 1.0.2b)
circuit board: 8.65078cm x 6.28341cm

parts:
  MH-ET_LIVE_ESP32_DEVKIT1 = MH-ET LIVE ESP32 DEVKIT 38 pins
  Part1 = Adafruit MAX31865 RTD Sensor Breakout [part_number="Adafruit #3328"]
  M1 = pt100 RTD
  S1 = SWITCH-MOMENTARY-2 [package=tactile-pth-12mm]

nets:
  3V3: MH-ET_LIVE_ESP32_DEVKIT1.3V3, Part1.VIN
  N1: MH-ET_LIVE_ESP32_DEVKIT1.GND#64, Part1.GND
  N2: MH-ET_LIVE_ESP32_DEVKIT1.IO23, Part1.SDI
  N3: MH-ET_LIVE_ESP32_DEVKIT1.GND#70, S1.1
  N4: MH-ET_LIVE_ESP32_DEVKIT1.IO19, Part1.SDO
  N5: MH-ET_LIVE_ESP32_DEVKIT1.IO18, Part1.SCLK
  N6: MH-ET_LIVE_ESP32_DEVKIT1.IO5, Part1.CS
  N7: MH-ET_LIVE_ESP32_DEVKIT1.IO0, S1.2
  N8: Part1.RTDIN+, Part1.FORCE+, M1.pin1, M1.pin2
  N9: Part1.RTDIN-, M1.pin3

custom parts:
  MH-ET LIVE ESP32 DEVKIT 38 pins: http://mh.nodebb.com/topic/2/mh-et-live-esp32-devkit
  Adafruit MAX31865 RTD Sensor Breakout: For precision temperature sensing, nothing beats a Platinum RTD. Resistance temperature detectors (RTDs) are temperature sensors that contain a resistor that changes resistance value as its temperature changes, basically a kind of thermistor. In this sensor, the resistor is actually a small strip of Platinum with a resistance of 100 ohms at 0°C, thus the name PT100. Compared to most NTC/PTC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
  pt100 RTD: CrocSee RTD Pt100 Temperature Sensor Probe 3 Wires 2M Cable Thermocouple -58~572°F (-50-300°C) 1/2" BSP Thread.
